# Fritzing sketch keyboard (saved by Fritzing 0.9.4)

parts:
  PICO_Microwriter_Keyboard_Controller = Raspberry Pi Pico  # not connected
  S9 = Round Pushbutton
  S10 = Round Pushbutton
  S11 = Round Pushbutton
  S12 = Round Pushbutton  # not connected
  S13 = Round Pushbutton
  S14 = Round Pushbutton
  S15 = Round Pushbutton
  S16 = Round Pushbutton

nets:
  N1: S9.leg1, S10.leg1, S11.leg1
  N2: S13.leg1, S14.leg1
  N3: S15.leg1, S16.leg1

custom parts:
  Raspberry Pi Pico: Raspberry Pi Pico. Based around the RP2040 microcontroller the Pico is a low cost microcontroller device bringing Raspberry Pi quality, cost, and easy of use to the microcontroller space. Jan 2021, Split part in to two versions: tht (this one) and SMD. This one will drill holes for a .1 in header in pcb to allow plugging in the module as well as providing pads to solder the module to the top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
